# Fritzing sketch fox-transmitter (saved by Fritzing 1.0.6)

parts:
  WeMos_D1_R32 = >Wemos D1 R32
  HM-TRLR-D = IC, SIP package, 11 pins [chip_label=HM-TRLR-D]
  SMA = SMA Antenna Connector  # not connected
  AA1 = Battery Holders [package=battery-aa]
  AA2 = Battery Holders [package=battery-aa]
  AA3 = Battery Holders [package=battery-aa]
  AA4 = Battery Holders [package=battery-aa]
  AA5 = Battery Holders [package=battery-aa]

nets:
  N1: WeMos_D1_R32.5V, HM-TRLR-D.pin4
  N2: WeMos_D1_R32.GND, HM-TRLR-D.pin3, HM-TRLR-D.pin10, AA5.+
  N3: WeMos_D1_R32.VN, AA1.-
  N4: WeMos_D1_R32.IO17, HM-TRLR-D.pin5
  N5: WeMos_D1_R32.IO16, HM-TRLR-D.pin6
  N6: WeMos_D1_R32.IO14, HM-TRLR-D.pin2
  N7: AA1.+, AA2.-
  N8: AA2.+, AA3.-
  N9: AA3.+, AA4.-
  N10: AA4.+, AA5.-

custom parts:
  >Wemos D1 R32: Wemos D1 R32 - This board is used with dual-mode Wi-Fi and Bluetooth chips, which is safe, reliable, and scalable to a variety of applications. DC in 5V-12V, 1 analog input(3.2V max input), a Micro USB connection, Compatible with D1 R32=WiFi+bluetooth+UNO
