# Fritzing sketch led-receiver (saved by Fritzing 1.0.6)

parts:
  ESP32_DevKit = ESP32-38PinWide
  R1 = Resistor [resistance=160Ω tolerance=±5% package=THT]
  LED1 = LED - 5mm [color="Red (633nm)" package="5 mm [THT]"]
  R2 = Resistor [resistance=160Ω tolerance=±5% package=THT]
  LED2 = LED - 5mm [color="Red (633nm)" package="5 mm [THT]"]
  R3 = Resistor [resistance=160Ω tolerance=±5% package=THT]
  LED3 = LED - 5mm [color="Yellow (585nm)" package="5 mm [THT]"]
  R4 = Resistor [resistance=160Ω tolerance=±5% package=THT]
  LED4 = LED - 5mm [color="Yellow (585nm)" package="5 mm [THT]"]
  R5 = Resistor [resistance=160Ω tolerance=±5% package=THT]
  LED5 = LED - 5mm [color="Yellow (585nm)" package="5 mm [THT]"]
  R6 = Resistor [resistance=30Ω tolerance=±5% package=THT]
  LED6 = LED - 5mm [color="Green (555nm)" package="5 mm [THT]"]
  R7 = Resistor [resistance=30Ω tolerance=±5% package=THT]
  LED7 = LED - 5mm [color="Green (555nm)" package="5 mm [THT]"]
  SW1 = Pushbutton [package="[THT]"]
  LoRa-E5 = IC, SIP package, 4 pins [chip_label=LoRa-E5]
  Charger = Adafruit bq25185 with 5V Boost Breakout
  Battery = LIPO-1000mAh [package=lipo-1000]
  Power = Toggle Switch [package=THT]

nets:
  N1: ESP32_DevKit.3.3, LoRa-E5.pin1
  N2: ESP32_DevKit.GPIO32, SW1.Pin_3
  N3: ESP32_DevKit.GPIO33, R1.Pin_0
  N4: ESP32_DevKit.GPIO25, R2.Pin_0
  N5: ESP32_DevKit.GPIO26, R3.Pin_0
  N6: ESP32_DevKit.GPIO27, R4.Pin_0
  N7: ESP32_DevKit.GPIO14, R5.Pin_0
  N8: ESP32_DevKit.GPIO12, R6.Pin_0
  GND: ESP32_DevKit.GND, LED1.cathode, LED2.cathode, LED3.cathode, LED4.cathode, LED5.cathode, LED6.cathode, LED7.cathode, SW1.Pin_2, LoRa-E5.pin2, Charger.GND, Battery.-
  N9: ESP32_DevKit.GPIO13, R7.Pin_0
  N10: ESP32_DevKit.VIN, Power.L2
  N11: ESP32_DevKit.GPIO16, LoRa-E5.pin4
  N12: ESP32_DevKit.GPIO17, LoRa-E5.pin3
  N13: R1.Pin_1, LED1.anode
  N14: R2.Pin_1, LED2.anode
  N15: R3.Pin_1, LED3.anode
  N16: R4.Pin_1, LED4.anode
  N17: R5.Pin_1, LED5.anode
  N18: R6.Pin_1, LED6.anode
  N19: R7.Pin_1, LED7.anode
  N20: Charger.VBAT, Battery.+
  N21: Charger.+5V, Power.COM

custom parts:
  ESP32-38PinWide: Generic 38-Pin ESP32 with wide format (only access to one side of pins on a breadboard) based on Stephen Lilley's HiLetgo ESP-WROOM-32 ESP32 ESP-32S Development Board.
